# Fritzing sketch at-me (saved by Fritzing 0.9.5d)
circuit board: 8.46667cm x 5.64444cm
breadboards: 2

parts:
  Componente1 = Arduino Nano (Rev3.0)
  DFRobot_DFPlayer_Mini1 = DFRobot DFPlayer Mini [part_number=DFR0299]
  S1 = Pushbutton [package="[THT]"]
  U2 = 3.5mm Audio Jack [package=audio-jack]
  R1 = Resistor [tolerance=±5% resistance=1k package=THT]
  LED1 = smd LED [color="Orange (612nm)" package="1206 [SMD]"]
  R2 = Resistor [tolerance=±5% resistance=220 package=THT]

nets (from the schematic view):
  N1: Componente1.GND, DFRobot_DFPlayer_Mini1.GND-1, DFRobot_DFPlayer_Mini1.GND-2, S1.Pin_1, S1.Pin_2, LED1.anode
  N2: Componente1.D2, R2.Pin_0
  N3: Componente1.D6, S1.Pin_3, S1.Pin_4
  N4: Componente1.D10, DFRobot_DFPlayer_Mini1.TX
  N5: Componente1.D11/MOSI, R1.Pin_0
  5V: Componente1.5V, DFRobot_DFPlayer_Mini1.VCC
  N6: DFRobot_DFPlayer_Mini1.RX, R1.Pin_1
  N7: DFRobot_DFPlayer_Mini1.SPK_1, U2.RIGHT, U2.SLEEVE
  N8: DFRobot_DFPlayer_Mini1.SPK_2, U2.LEFT
  N9: LED1.cathode, R2.Pin_1
